// Logisim project adc_simulation.circ as structural Verilog: 1 circuit, main circuit main
module main (
  input  v1,
  input  v2,
  input  v3,
  output b2,
  output b1,
  output b0
);

  and and_1 (b2, v1, v2);
  and and_2 (b1, v2, v3);

  assign b0 = v3;
endmodule
